// Logisim project project.circ as structural Verilog: 1 circuit, main circuit main
module main (
  input  [2:0] in_1,
  input  [2:0] in_2,
  output A_B,
  output A_B_2,
  output A_B_3
);

  wire and_1_out, and_2_out, and_3_out, and_4_out, and_5_out, and_6_out, not_1_out, not_2_out, not_3_out,
       not_4_out, not_5_out, not_6_out, xnor_1_out, xnor_2_out, xnor_3_out;

  not not_1 (not_1_out, in_1[2]);
  not not_2 (not_2_out, in_2[2]);
  not not_3 (not_3_out, in_1[1]);
  not not_4 (not_4_out, in_2[1]);
  not not_5 (not_5_out, in_1[0]);
  not not_6 (not_6_out, in_2[0]);
  and and_1 (and_1_out, in_1[2], not_2_out);
  and and_2 (and_2_out, in_2[2], not_1_out);
  xnor xnor_1 (xnor_1_out, in_1[2], in_2[2]);
  xnor xnor_2 (xnor_2_out, in_1[1], in_2[1]);
  xnor xnor_3 (xnor_3_out, in_2[0], in_1[0]);
  and and_3 (and_3_out, xnor_1_out, in_1[1], not_4_out);
  and and_4 (and_4_out, xnor_1_out, not_6_out, in_1[0], xnor_2_out);
  and and_5 (and_5_out, xnor_1_out, in_2[1], not_3_out);
  and and_6 (and_6_out, xnor_1_out, xnor_2_out, in_2[0], not_5_out);
  and and_7 (A_B_3, xnor_2_out, xnor_1_out, xnor_3_out);
  or or_1 (A_B, and_1_out, and_3_out, and_4_out);
  or or_2 (A_B_2, and_2_out, and_5_out, and_6_out);

  // Notes on the sheet:
  //   A2
  //   B2
  //   A1
  //   B1
  //   A0
  //   B0
endmodule
